# Fritzing sketch chillipowerboard (saved by Fritzing 0.8.3b)
stripboards: 1

parts:
  Part1 = Arduino Pro Mini v13
  D1 = Schottky Diode [part_number=1N5817 breakdown_voltage=3.6V package="300 mil [THT]"]
  IC1 = IC, DIP package, 8 pins [chip_label=RTC]
  XTAL1 = CRYSTAL - kHz [frequency="32 kHz"]
  D2 = Schottky Diode [part_number=1N5817 package="300 mil [THT]"]
  J1 = molex pin header, 2 pins [form=molex]
  BAT1 = Battery Holders [package=battcom_20mm_pth]
  J2 = Piezo Speaker
  R1 = Resistor [tolerance=±5% resistance=100 package=THT]
  Part3 = Bluetooth Mate Silver

nets:
  N1: Part1.GND, J2.pin1
  N2: Part1.A4, IC1.pin5
  N3: Part1.A5, IC1.pin6
  N4: Part1.D9_PWM, R1.Pin_0
  N5: Part1.D1/RX, Part3.TX_5V
  N6: Part1.D0/TX, Part3.RX_5V
  N7: D1.cathode, IC1.pin8, D2.cathode
  N8: IC1.pin1, XTAL1.pin_1
  N9: IC1.pin2, XTAL1.pin_0
  N10: IC1.pin3, IC1.pin4
  N11: D2.anode, J1.pin2
  N12: J1.pin1, BAT1.-

notes:
  To DX Relay Board
  To DC 5V PSU
  3V CR2032
  JY MCU V1.05
  5V
